// Logisim project IR.circ as structural Verilog: 2 circuits, main circuit main
module main (
  input  [15:0] in_1,
  output [15:0] out_2
);

  wire clock_1_out;

  Register register_1 (.Data_In(in_1[3:0]), .Clock(clock_1_out), .Data_Out(out_2[3:0]));
  Register register_2 (.Data_In(in_1[7:4]), .Clock(clock_1_out), .Data_Out(out_2[7:4]));
  Register register_3 (.Data_In(in_1[11:8]), .Clock(clock_1_out), .Data_Out(out_2[11:8]));
  Register register_4 (.Data_In(in_1[15:12]), .Clock(clock_1_out), .Data_Out(out_2[15:12]));
  Clock clock_1 (.out(clock_1_out));
endmodule

module Register (
  input  [3:0] Data_In,
  input  Clock,
  output [3:0] Data_Out
);

  D_Flip_Flop d_ff_1 (.clk(Clock), .D(Data_In[0]), .Q(Data_Out[0]));  // open: Qn, preset, en, reset
  D_Flip_Flop d_ff_2 (.clk(Clock), .D(Data_In[1]), .Q(Data_Out[1]));  // open: Qn, preset, en, reset
  D_Flip_Flop d_ff_3 (.clk(Clock), .D(Data_In[2]), .Q(Data_Out[2]));  // open: Qn, preset, en, reset
  D_Flip_Flop d_ff_4 (.clk(Clock), .D(Data_In[3]), .Q(Data_Out[3]));  // open: Qn, preset, en, reset
endmodule
