// Logisim project Instruction Memory.circ as structural Verilog: 3 circuits, main circuit main
module main (
  input  Activate,
  input  [15:0] Data_In,
  output [15:0] Data_Out
);

  Register register_1 (.Data_In(Data_In[3:0]), .Clock(Activate), .Data_Out(Data_Out[3:0]));
  Register register_2 (.Data_In(Data_In[7:4]), .Clock(Activate), .Data_Out(Data_Out[7:4]));
  Register register_3 (.Data_In(Data_In[11:8]), .Clock(Activate), .Data_Out(Data_Out[11:8]));
  Register register_4 (.Data_In(Data_In[15:12]), .Clock(Activate), .Data_Out(Data_Out[15:12]));
endmodule

module Register (
  input  [3:0] Data_In,
  input  Clock,
  output [3:0] Data_Out
);

  D_Flip_Flop d_ff_1 (.clk(Clock), .D(Data_In[0]), .Q(Data_Out[0]));  // open: Qn, preset, en, reset
  D_Flip_Flop d_ff_2 (.clk(Clock), .D(Data_In[1]), .Q(Data_Out[1]));  // open: Qn, preset, en, reset
  D_Flip_Flop d_ff_3 (.clk(Clock), .D(Data_In[2]), .Q(Data_Out[2]));  // open: Qn, preset, en, reset
  D_Flip_Flop d_ff_4 (.clk(Clock), .D(Data_In[3]), .Q(Data_Out[3]));  // open: Qn, preset, en, reset
endmodule

module Instruction_Memory (
  input  [3:0] Adress_to_Write,
  input  Write_State,
  input  [15:0] Data_to_Save,
  input  [3:0] Adress_to_Read,
  output [15:0] Data_to_Read
);

  wire [15:0] _0000_data_out, _0001_data_out, _0010_data_out, _0011_data_out, _0100_data_out, _0101_data_out,
       _0110_data_out, _0111_data_out, _1000_data_out, _1001_data_out, _1010_data_out, _1011_data_out,
       _1100_data_out, _1101_data_out, _1110_data_out, _1111_data_out, demultiplexer_1_out0,
       demultiplexer_1_out1, demultiplexer_1_out2, demultiplexer_1_out3, demultiplexer_1_out4,
       demultiplexer_1_out5, demultiplexer_1_out6, demultiplexer_1_out7, demultiplexer_1_out8,
       demultiplexer_1_out9, demultiplexer_1_out10, demultiplexer_1_out11, demultiplexer_1_out12,
       demultiplexer_1_out13, demultiplexer_1_out14, demultiplexer_1_out15;

  Demultiplexer #(.select(4), .width(16), .tristate("true"), .enable("false")) demultiplexer_1 (
    .out0(demultiplexer_1_out0), .out1(demultiplexer_1_out1), .out2(demultiplexer_1_out2),
    .out3(demultiplexer_1_out3), .out4(demultiplexer_1_out4), .out5(demultiplexer_1_out5),
    .out6(demultiplexer_1_out6), .out7(demultiplexer_1_out7), .out8(demultiplexer_1_out8),
    .out9(demultiplexer_1_out9), .out10(demultiplexer_1_out10), .out11(demultiplexer_1_out11),
    .out12(demultiplexer_1_out12), .out13(demultiplexer_1_out13), .out14(demultiplexer_1_out14),
    .out15(demultiplexer_1_out15), .in(Data_to_Save), .sel(Adress_to_Write));
  main _0000 (.Data_In(demultiplexer_1_out0), .Data_Out(_0000_data_out), .Activate(Write_State));
  main _0001 (.Data_In(demultiplexer_1_out1), .Data_Out(_0001_data_out), .Activate(Write_State));
  main _0010 (.Data_In(demultiplexer_1_out2), .Data_Out(_0010_data_out), .Activate(Write_State));
  main _0011 (.Data_In(demultiplexer_1_out3), .Data_Out(_0011_data_out), .Activate(Write_State));
  main _0100 (.Data_In(demultiplexer_1_out4), .Data_Out(_0100_data_out), .Activate(Write_State));
  main _0101 (.Data_In(demultiplexer_1_out5), .Data_Out(_0101_data_out), .Activate(Write_State));
  main _0110 (.Data_In(demultiplexer_1_out6), .Data_Out(_0110_data_out), .Activate(Write_State));
  main _0111 (.Data_In(demultiplexer_1_out7), .Data_Out(_0111_data_out), .Activate(Write_State));
  main _1000 (.Data_In(demultiplexer_1_out8), .Data_Out(_1000_data_out), .Activate(Write_State));
  main _1001 (.Data_In(demultiplexer_1_out9), .Data_Out(_1001_data_out), .Activate(Write_State));
  main _1010 (.Data_In(demultiplexer_1_out10), .Data_Out(_1010_data_out), .Activate(Write_State));
  main _1011 (.Data_In(demultiplexer_1_out11), .Data_Out(_1011_data_out), .Activate(Write_State));
  main _1100 (.Data_In(demultiplexer_1_out12), .Data_Out(_1100_data_out), .Activate(Write_State));
  main _1101 (.Data_In(demultiplexer_1_out13), .Data_Out(_1101_data_out), .Activate(Write_State));
  main _1110 (.Data_In(demultiplexer_1_out14), .Data_Out(_1110_data_out), .Activate(Write_State));
  main _1111 (.Data_In(demultiplexer_1_out15), .Data_Out(_1111_data_out), .Activate(Write_State));
  Multiplexer #(.select(4), .width(16), .enable("false")) multiplexer_1 (
    .in0(_0000_data_out), .in1(_0001_data_out), .in2(_0010_data_out), .in3(_0011_data_out),
    .in4(_0100_data_out), .in5(_0101_data_out), .in6(_0110_data_out), .in7(_0111_data_out),
    .in8(_1000_data_out), .in9(_1001_data_out), .in10(_1010_data_out), .in11(_1011_data_out),
    .in12(_1100_data_out), .in13(_1101_data_out), .in14(_1110_data_out), .in15(_1111_data_out),
    .out(Data_to_Read), .sel(Adress_to_Read));
endmodule
