// Logisim project JumpDecoder.circ as structural Verilog: 1 circuit, main circuit main
module main (
  input  Is_Jump_Instruction,
  input  [2:0] Gambiarra_do_estado,
  input  [3:0] PC,
  input  [3:0] RA,
  output [3:0] out_5
);

  wire comparator_1_eq, comparator_2_eq;
  wire [3:0] adder_1_out, adder_2_out, multiplexer_1_out, multiplexer_2_out;

  Comparator #(.width(3), .mode("unsigned")) comparator_1 (
    .a(Gambiarra_do_estado), .b(3'b000), .eq(comparator_1_eq));  // open: gt, lt
  Adder #(.width(4)) adder_1 (.a(PC), .b(4'b0001), .out(adder_1_out));  // open: cin, cout
  Adder #(.width(4)) adder_2 (.a(PC), .b(RA), .out(adder_2_out));  // open: cin, cout
  Multiplexer #(.width(4), .enable("false")) multiplexer_1 (
    .in0(adder_1_out), .in1(adder_2_out), .out(multiplexer_1_out), .sel(Is_Jump_Instruction));
  Comparator #(.width(4), .mode("unsigned")) comparator_2 (.a(PC), .b(4'b1111), .eq(comparator_2_eq));  // open: gt, lt
  Multiplexer #(.width(4), .enable("false")) multiplexer_2 (
    .in0(multiplexer_1_out), .in1(4'b0000), .out(multiplexer_2_out), .sel(comparator_2_eq));
  Multiplexer #(.width(4), .enable("false")) multiplexer_3 (
    .in0(multiplexer_2_out), .in1(PC), .out(out_5), .sel(comparator_1_eq));

  // Notes on the sheet:
  //   <!--Gambiarra enxuta!!!-->
endmodule
