// Logisim project MoveDecoder.circ as structural Verilog: 1 circuit, main circuit main
module main (
  input  [2:0] Estado,
  input  [3:0] Operandos,
  input  Clock_R1,
  input  Clock_R0,
  input  [3:0] R0_data,
  input  [3:0] RA,
  input  [3:0] R1_data,
  output Clock_R1_Output,
  output Clock_R0_Output,
  output [3:0] Output_R0,
  output [3:0] Output_R1
);

  wire and_1_out, and_2_out, comparator_1_eq, comparator_2_eq, comparator_3_eq;
  wire [1:0] multiplexer_1_out, multiplexer_2_out;

  Comparator #(.width(3)) comparator_1 (.a(Estado), .b(3'b101), .eq(comparator_1_eq));  // open: gt, lt
  Multiplexer #(.width(2), .enable("false")) multiplexer_1 (
    .in0(2'b00), .in1(Operandos[3:2]), .out(multiplexer_1_out), .sel(comparator_1_eq));
  Multiplexer #(.width(2), .enable("false")) multiplexer_2 (
    .in0(2'b00), .in1(Operandos[3:2]), .out(multiplexer_2_out), .sel(comparator_1_eq));
  Comparator #(.width(2), .mode("unsigned")) comparator_2 (
    .a(multiplexer_2_out), .b(2'b10), .eq(comparator_2_eq));  // open: gt, lt
  Comparator #(.width(2), .mode("unsigned")) comparator_3 (
    .a(multiplexer_1_out), .b(2'b01), .eq(comparator_3_eq));  // open: gt, lt
  and and_1 (and_1_out, comparator_2_eq, Clock_R1);
  and and_2 (and_2_out, comparator_3_eq, Clock_R0);
  Multiplexer #(.enable("false")) multiplexer_3 (
    .in0(Clock_R1), .in1(and_1_out), .out(Clock_R1_Output), .sel(comparator_1_eq));
  Multiplexer #(.enable("false")) multiplexer_4 (
    .in0(Clock_R0), .in1(and_2_out), .out(Clock_R0_Output), .sel(comparator_1_eq));
  Multiplexer #(.width(4), .enable("false")) multiplexer_5 (
    .in0(R0_data), .in1(RA), .out(Output_R0), .sel(comparator_1_eq));
  Multiplexer #(.width(4), .enable("false")) multiplexer_6 (
    .in0(R1_data), .in1(RA), .out(Output_R1), .sel(comparator_1_eq));

  // Notes on the sheet:
  //   RD
  //   Verifica se o destino é o R1 
  //   Verifica se o destino é o R0 
endmodule
