// Logisim project Register.circ as structural Verilog: 1 circuit, main circuit Register
module Register (
  input  [3:0] Data_In,
  input  Clock,
  output [3:0] Data_Out
);

  D_Flip_Flop d_ff_1 (.clk(Clock), .D(Data_In[0]), .Q(Data_Out[0]));  // open: Qn, preset, en, reset
  D_Flip_Flop d_ff_2 (.clk(Clock), .D(Data_In[1]), .Q(Data_Out[1]));  // open: Qn, preset, en, reset
  D_Flip_Flop d_ff_3 (.clk(Clock), .D(Data_In[2]), .Q(Data_Out[2]));  // open: Qn, preset, en, reset
  D_Flip_Flop d_ff_4 (.clk(Clock), .D(Data_In[3]), .Q(Data_Out[3]));  // open: Qn, preset, en, reset
endmodule
