// Logisim project SelectDataMemory.circ as structural Verilog: 1 circuit, main circuit main
module main (
  input  [15:0] Instruction,
  input  [2:0] Estado,
  input  [3:0] R0,
  input  [3:0] R1,
  output [15:0] out_5
);

  wire comparator_1_eq, comparator_2_eq;
  wire [3:0] multiplexer_1_out;
  wire [15:0] bit_extender_1_out;

  Comparator #(.width(3), .mode("unsigned")) comparator_1 (
    .a(Estado), .b(3'b110), .eq(comparator_1_eq));  // open: gt, lt
  Comparator #(.width(2), .mode("unsigned")) comparator_2 (
    .a(Instruction[9:8]), .b(2'b10), .eq(comparator_2_eq));  // open: gt, lt
  Multiplexer #(.width(4), .enable("false")) multiplexer_1 (
    .in0(R0), .in1(R1), .out(multiplexer_1_out), .sel(comparator_2_eq));
  assign bit_extender_1_out = {{12{1'b0}}, multiplexer_1_out};  // Bit_Extender bit_extender_1
  Multiplexer #(.width(16), .enable("false")) multiplexer_2 (
    .in0(Instruction), .in1(bit_extender_1_out), .out(out_5), .sel(comparator_1_eq));

  // Notes on the sheet:
  //   RS
  //   Se é escrita
  //   Verifica se o destino é o R1 
endmodule
