// Logisim project Ula.circ as structural Verilog: 4 circuits, main circuit sequencer
module sequencer (
  input  [3:0] estado_atual,
  input  [3:0] opcode,
  input  [3:0] Output_send,
  output [3:0] out_4
);

  wire and_1_out, and_2_out, and_3_out, and_4_out, and_5_out, and_6_out, atype_1_is_type_a,
       atype_2_is_type_a, comparator_1_eq, comparator_2_eq, comparator_3_eq, comparator_4_eq,
       comparator_5_eq, comparator_6_eq, comparator_7_eq, comparator_8_eq, comparator_9_eq, comparator_10_eq,
       comparator_11_eq, comparator_12_eq, jtype_1_is_type_j, or_1_out, or_2_out;

  AType atype_1 (.Opcode(opcode), .Is_Type_A(atype_1_is_type_a));
  AType atype_2 (.Opcode(opcode), .Is_Type_A(atype_2_is_type_a));
  JType jtype_1 (.Opcode(opcode), .Is_Type_J(jtype_1_is_type_j));
  Comparator #(.width(4), .mode("unsigned")) comparator_1 (
    .a(opcode), .b(4'b0000), .eq(comparator_1_eq));  // open: gt, lt
  Comparator #(.width(4), .mode("unsigned")) comparator_2 (
    .a(opcode), .b(4'b0100), .eq(comparator_2_eq));  // open: gt, lt
  Comparator #(.width(4), .mode("unsigned")) comparator_3 (
    .a(estado_atual), .b(4'b0100), .eq(comparator_3_eq));  // open: gt, lt
  Comparator #(.width(4), .mode("unsigned")) comparator_4 (
    .a(estado_atual), .b(4'b0101), .eq(comparator_4_eq));  // open: gt, lt
  Comparator #(.width(4), .mode("unsigned")) comparator_5 (
    .a(estado_atual), .b(4'b0111), .eq(comparator_5_eq));  // open: gt, lt
  Comparator #(.width(4), .mode("unsigned")) comparator_6 (
    .a(estado_atual), .b(4'b1000), .eq(comparator_6_eq));  // open: gt, lt
  Comparator #(.width(4), .mode("unsigned")) comparator_7 (
    .a(estado_atual), .b(4'b1001), .eq(comparator_7_eq));  // open: gt, lt
  Comparator #(.width(4), .mode("unsigned")) comparator_8 (
    .a(estado_atual), .b(4'b0000), .eq(comparator_8_eq));  // open: gt, lt
  Comparator #(.width(4), .mode("unsigned")) comparator_9 (
    .a(estado_atual), .b(4'b0011), .eq(comparator_9_eq));  // open: gt, lt
  Comparator #(.width(4), .mode("unsigned")) comparator_10 (
    .a(estado_atual), .b(4'b0110), .eq(comparator_10_eq));  // open: gt, lt
  Comparator #(.width(4), .mode("unsigned")) comparator_11 (
    .a(estado_atual), .b(4'b0010), .eq(comparator_11_eq));  // open: gt, lt
  Comparator #(.width(4), .mode("unsigned")) comparator_12 (
    .a(estado_atual), .b(4'b0001), .eq(comparator_12_eq));  // open: gt, lt
  or or_1 (or_1_out, comparator_1_eq, atype_1_is_type_a);
  and and_1 (and_1_out, comparator_1_eq, comparator_11_eq);
  and and_2 (and_2_out, comparator_11_eq, atype_1_is_type_a);
  and and_3 (and_3_out, or_1_out, comparator_12_eq);
  and and_4 (and_4_out, comparator_12_eq, atype_2_is_type_a);
  and and_5 (and_5_out, comparator_12_eq, comparator_2_eq);
  and and_6 (and_6_out, comparator_12_eq, jtype_1_is_type_j);
  or or_2 (or_2_out, comparator_3_eq, comparator_4_eq, comparator_5_eq, comparator_6_eq, comparator_7_eq);
  Priority_Encoder #(.select(4), .disabled(0)) priority_encoder_1 (
    .in0(or_2_out), .in1(comparator_8_eq), .in2(and_3_out), .in3(and_1_out), .in4(comparator_9_eq),
    .in5(and_2_out), .in6(and_4_out), .in7(comparator_10_eq), .in8(and_5_out), .in9(and_6_out), .in10(1'b0),
    .in11(1'b0), .in12(1'b0), .in13(1'b0), .in14(1'b0), .in15(1'b0), .out(out_4), .en_in(1'b1));  // open: gs, en_out

  assign Output_send = estado_atual;

  // Notes on the sheet:
  //   LW
  //   SW
  //   A-Type
  //   BEQ
  //   J-Type
  //   Estados
endmodule

module AType (
  input  [3:0] Opcode,
  output Is_Type_A
);

  wire comparator_1_gt, comparator_2_lt;

  Comparator #(.width(4), .mode("unsigned")) comparator_1 (
    .a(Opcode), .b(4'b0000), .gt(comparator_1_gt));  // open: eq, lt
  Comparator #(.width(4), .mode("unsigned")) comparator_2 (
    .a(Opcode), .b(4'b1101), .lt(comparator_2_lt));  // open: gt, eq
  and and_1 (Is_Type_A, comparator_1_gt, comparator_2_lt);
endmodule

module JType (
  input  [3:0] Opcode,
  output Is_Type_J
);

  wire comparator_1_gt, comparator_2_eq, comparator_2_lt, or_1_out;

  Comparator #(.width(4), .mode("unsigned")) comparator_1 (
    .a(Opcode), .b(4'b1100), .gt(comparator_1_gt));  // open: eq, lt
  Comparator #(.width(4), .mode("unsigned")) comparator_2 (
    .a(Opcode), .b(4'b1111), .eq(comparator_2_eq), .lt(comparator_2_lt));  // open: gt
  or or_1 (or_1_out, comparator_2_eq, comparator_2_lt);
  and and_1 (Is_Type_J, comparator_1_gt, or_1_out);
endmodule

module Send_Signal (
  input  [3:0] in_1,
  input  [3:0] in_2,
  input  [15:0] in_3,
  output [3:0] state
);

  wire comparator_1_eq, comparator_2_eq, comparator_3_eq, comparator_4_eq, comparator_5_eq, comparator_6_eq,
       comparator_7_eq, comparator_8_eq, comparator_9_eq;
  wire [3:0] undriven;

  sequencer Sequencer (.estado_atual(in_1), .opcode(in_2), .Output_send(undriven), .out_4(state));
  Comparator #(.width(4), .mode("unsigned")) comparator_1 (
    .a(undriven), .b(4'b0001), .eq(comparator_1_eq));  // open: gt, lt
  Comparator #(.width(4), .mode("unsigned")) comparator_2 (
    .a(undriven), .b(4'b0010), .eq(comparator_2_eq));  // open: gt, lt
  Comparator #(.width(4), .mode("unsigned")) comparator_3 (
    .a(undriven), .b(4'b0011), .eq(comparator_3_eq));  // open: gt, lt
  Comparator #(.width(4), .mode("unsigned")) comparator_4 (
    .a(undriven), .b(4'b0100), .eq(comparator_4_eq));  // open: gt, lt
  Comparator #(.width(4), .mode("unsigned")) comparator_5 (
    .a(undriven), .b(4'b0101), .eq(comparator_5_eq));  // open: gt, lt
  Comparator #(.width(4), .mode("unsigned")) comparator_6 (
    .a(undriven), .b(4'b0110), .eq(comparator_6_eq));  // open: gt, lt
  Comparator #(.width(4), .mode("unsigned")) comparator_7 (
    .a(undriven), .b(4'b0111), .eq(comparator_7_eq));  // open: gt, lt
  Comparator #(.width(4), .mode("unsigned")) comparator_8 (
    .a(undriven), .b(4'b1000), .eq(comparator_8_eq));  // open: gt, lt
  Comparator #(.width(4), .mode("unsigned")) comparator_9 (
    .a(undriven), .b(4'b1001), .eq(comparator_9_eq));  // open: gt, lt

  // Notes on the sheet:
  //   Opcode
  //   AluSrcB
  //   AluSrcA
endmodule
