// Logisim project somador 3 bits.circ as structural Verilog: 1 circuit, main circuit main
module main (
  input  carry_in,
  input  \_1º_bit ,
  input  \_1º_bit_2 ,
  input  \_2º_bit ,
  input  \_2º_bit_2 ,
  input  \_3º_bit ,
  input  \_3º_bit_2 ,
  output out_8,
  output bit_1,
  output bit_2,
  output overflow
);

  wire and_1_out, and_2_out, and_3_out, and_4_out, and_5_out, and_6_out, and_7_out, and_8_out, and_9_out,
       or_1_out, or_2_out, xor_1_out, xor_3_out, xor_5_out;

  xor xor_1 (xor_1_out, \_1º_bit , \_1º_bit_2 );
  and and_1 (and_1_out, \_1º_bit_2 , carry_in);
  and and_2 (and_2_out, \_1º_bit_2 , carry_in);
  and and_3 (and_3_out, \_1º_bit , \_1º_bit_2 );
  xor xor_2 (out_8, xor_1_out, carry_in);
  or or_1 (or_1_out, and_1_out, and_2_out, and_3_out);
  xor xor_3 (xor_3_out, \_2º_bit , \_2º_bit_2 );
  and and_4 (and_4_out, \_2º_bit_2 , or_1_out);
  and and_5 (and_5_out, \_2º_bit_2 , or_1_out);
  and and_6 (and_6_out, \_2º_bit , \_2º_bit_2 );
  xor xor_4 (bit_1, xor_3_out, or_1_out);
  or or_2 (or_2_out, and_4_out, and_5_out, and_6_out);
  xor xor_5 (xor_5_out, \_3º_bit , \_3º_bit_2 );
  and and_7 (and_7_out, \_3º_bit_2 , or_2_out);
  and and_8 (and_8_out, \_3º_bit_2 , or_2_out);
  and and_9 (and_9_out, \_3º_bit , \_3º_bit_2 );
  or or_3 (overflow, and_7_out, and_8_out, and_9_out);
  xor xor_6 (bit_2, xor_5_out, or_2_out);

  // Notes on the sheet:
  //   bit menos significativo
  //   carry out do anterior e carry in do próximo
  //   carry out do anterior e carry in do próximo
endmodule
